// Digital circuit instruction_memory.dig as structural Verilog
module instruction_memory (
  input  [5:0] A,
  input  [3:0] PN,
  output [31:0] D
);

  wire [31:0] Fibonacci_Iter_12_d, rom_1_d, rom_2_d;

  ROM #(.AddrBits(6), .Bits(32)) Fibonacci_Iter_12 (.A(A), .sel(1'b1), .D(Fibonacci_Iter_12_d));
  ROM #(.AddrBits(6), .Bits(32)) rom_1 (.A(A), .sel(1'b1), .D(rom_1_d));
  ROM #(.AddrBits(6), .Bits(32)) rom_2 (.A(A), .sel(1'b1), .D(rom_2_d));
  Multiplexer #(.Selector_Bits(4), .Bits(32)) multiplexer_1 (
    .sel(PN), .in_0(Fibonacci_Iter_12_d), .in_1(rom_1_d), .in_2(rom_2_d), .in_3({32{1'b0}}),
    .in_4({32{1'b0}}), .in_5({32{1'b0}}), .in_6({32{1'b0}}), .in_7({32{1'b0}}), .in_8({32{1'b0}}),
    .in_9({32{1'b0}}), .in_10({32{1'b0}}), .in_11({32{1'b0}}), .in_12({32{1'b0}}), .in_13({32{1'b0}}),
    .in_14({32{1'b0}}), .in_15({32{1'b0}}), .out(D));

  // Notes on the sheet:
  //   contents of Fibonacci_Iter_12 (hex, n*v repeats v):
  //   e3a0000c,eb000001,eaffffff,eafffffe,e3a01001,e3a02000,e3a03000,e3a04001,e3500000,
  //   a000008,e1510000,a000004,e1a02003,e1a03004,e0824003,e2811001,eafffff8,e1a00004,e12fff1e,
  //   e12fff1e
  //   contents of rom_1 (hex, n*v repeats v):
  //   e3a00000,eb000010,e1a04000,e3a00001,eb00000d,e1a05000,e3a00002,eb00000a,e1a06000,
  //   e3a00003,eb000007,e1a07000,e3a0000a,eb000004,e1a08000,e3a00013,eb000001,e1a09000,
  //   eafffffe,e3a01001,e3a02000,e3a03000,e3a04001,e3500000,a000008,e1510000,a000004,e1a02003,
  //   e1a03004,e0824003,e2811001,eafffff8,e1a00004,e12fff1e,e12fff1e
  //   contents of rom_2 (hex, n*v repeats v):
  //   e3a0d080,e24dd00c,e3a00001,e58d0000,e3a00002,e58d0004,e3a00003,e58d0008,e1a0000d,
  //   e3a01003,eb000000,eafffffe,e3a02000,e3a03000,e1520001,a000004,e590c000,e083300c,e2822001,
  //   e2800004,eafffff8,e1a00003,e12fff1e
endmodule
